# Fritzing sketch RaspberryPiKY040 (saved by Fritzing 0.9.2b)
breadboards: 1

parts:
  Raspberry_Pi1 = Raspberry Pi B+
  SW1 = ENCODER_RGB_CA [package=encoder_led_3]

nets:
  3V3: Raspberry_Pi1.3v3, Raspberry_Pi1.3V3, Raspberry_Pi1.5V, SW1.+
  N1: Raspberry_Pi1.GPIO5, SW1.C
  N2: Raspberry_Pi1.GPIO6, SW1.B
  N3: Raspberry_Pi1.GPIO13, SW1.A
  N4: Raspberry_Pi1.GND, SW1.-B
